# Fritzing sketch co2-detector (saved by Fritzing 0.9.3b)
breadboards: 1

parts:
  Part1 = Arduino Uno (Rev3)
  LCD1 = LCD screen
  DHT1 = DHT22 Humidity and Temperature Sensor
  TD-er1 = MH-Z19 CO2 sensor [part_number=MH-Z19]
  LCM1602_IIC2 = LCM1602 IIC [part_number="LCM1602 IIC" chip_label="LCM1602 IIC" package="DIP (Dual Inline) [THT]"]
  Mod1 = Passive Buzzer

nets:
  N1: Part1.A4/SDA, LCM1602_IIC2.SDA
  N2: Part1.A5/SCL, LCM1602_IIC2.SCL
  N3: Part1.D9_PWM, Mod1.S
  N4: Part1.D2, TD-er1.TX
  N5: Part1.D3_PWM, TD-er1.RX
  N6: Part1.D7, DHT1.DATA
  5V: Part1.5V, DHT1.VDD, TD-er1.Vin, LCM1602_IIC2.VCC
  GND: Part1.GND, DHT1.GND, TD-er1.GND, LCM1602_IIC2.GND, Mod1.-
  VDD: LCD1.VDD, LCM1602_IIC2.VDD
  N7: LCD1.V0, LCM1602_IIC2.V0
  N8: LCD1.RS, LCM1602_IIC2.RS
  N9: LCD1.R/W, LCM1602_IIC2.RW
  N10: LCD1.E, LCM1602_IIC2.E
  N11: LCD1.DB0, LCM1602_IIC2.D0
  N12: LCD1.DB1, LCM1602_IIC2.D1
  N13: LCD1.DB2, LCM1602_IIC2.D2
  N14: LCD1.DB3, LCM1602_IIC2.D3
  N15: LCD1.DB4, LCM1602_IIC2.D4
  N16: LCD1.DB5, LCM1602_IIC2.D5
  N17: LCD1.DB6, LCM1602_IIC2.D6
  N18: LCD1.DB7, LCM1602_IIC2.D7
  N19: LCD1.LED+, LCM1602_IIC2.A
  N20: LCD1.LED-, LCM1602_IIC2.K

custom parts:
  LCM1602 IIC: I2C-Module to use a 1602 or 2004 LCD on with the wire.h libory Serial LCD Modul
